# Fritzing sketch wiring_driver (saved by Fritzing 0.9.3b)

parts:
  Bauteil1 = Arduino Nano (Rev3.0)
  Pololu_A1 = Pololu A4988 [package=SO16]
  M1 = Stepper Motor - Bipolar
  Power_plug1 = Power plug

nets:
  N1: Bauteil1.D4, Pololu_A1.RESET
  N2: Bauteil1.D5, Pololu_A1.DIR
  N3: Bauteil1.D6, Pololu_A1.STEP
  N4: Pololu_A1.1B, M1.D
  N5: Pololu_A1.1A, M1.B
  N6: Pololu_A1.2A, M1.C
  N7: Pololu_A1.2B, M1.A
  GND: Pololu_A1.GND, Power_plug1.GND
  N8: Pololu_A1.VMOT, Power_plug1.VCC
